# Fritzing sketch Scheme (saved by Fritzing 0.9.10b)
circuit board: 8.46667cm x 5.64444cm
breadboards: 2

parts:
  ESP32 = MH-ET LIVE ESP32 DEVKIT 38 pins
  R1 = Resistor [tolerance=±5% power=0.25 resistance=1k package=THT]
  2N2222A = NPN-Transistor [package="TO92 [THT]"]
  Thermo_Couple_MAX31855 = Adafruit Thermocouple Amplifier MAX31855 [part_number="Adafruit #269"]
  I2C_16x2_LCD = female pin header, 4 pins [form="♀ (female)"]
  Solid_State = female pin header, 2 pins [form="♀ (female)"]
  D1_1N4001 = Diode [package=diode-hv]

nets:
  3V3: ESP32.3V3, Thermo_Couple_MAX31855.VIN
  N1: ESP32.IO25, Thermo_Couple_MAX31855.DO
  N2: ESP32.IO26, Thermo_Couple_MAX31855.CS
  N3: ESP32.IO27, Thermo_Couple_MAX31855.CLK
  N4: ESP32.5V, I2C_16x2_LCD.pin2, Solid_State.pin2, D1_1N4001.C
  GND: ESP32.GND#64, 2N2222A.E, Thermo_Couple_MAX31855.GND, I2C_16x2_LCD.pin1
  N5: ESP32.IO23, R1.Pin_0
  SDA I2C: ESP32.IO22, I2C_16x2_LCD.pin3
  SCL I2C: ESP32.IO21, I2C_16x2_LCD.pin4
  N6: R1.Pin_1, 2N2222A.B
  N7: 2N2222A.C, Solid_State.pin1, D1_1N4001.A

notes:
  SLC
  GND
  VCC 5V
  SDA
  gnd
  5vcc
  sda
  scl

custom parts:
  MH-ET LIVE ESP32 DEVKIT 38 pins: http://mh.nodebb.com/topic/2/mh-et-live-esp32-devkit
  Adafruit Thermocouple Amplifier MAX31855: Thermocouples are very sensitive, requiring a good amplifier with a cold-compensation reference. The MAX31855K does everything for you, and can be easily interfaced with any microcontroller, even one without an analog input. This breakout board has the chip itself, a 3.3V regulator with 10uF bypass capacitors and level shifting circuitry, all assembled and tested. Comes with a 2 pin terminal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
